# Fritzing sketch mywatch_final_v1 (saved by Fritzing 0.9.3b)
circuit board: 6.9206cm x 7.23707cm
breadboards: 2

parts:
  J5 = DS3232 Real Time clock [form="♀ (female)" package=THT]
  PIC18(L)F1 = PIC16(L)F1824 [chip_label=PIC16(L)F1824 package="DIP (Dual Inline) [THT]"]
  Part1 = Arduino Pro Mini v13
  J1 = EPD Adapter [form="♂ (shrouded male)" package=THT]
  J7 = Generic female header - 2 pins [form="♀ (female)" package=THT]
  J8 = female pin header, 2 pins [form="♀ (female)"]
  R1 = Resistor [tolerance=±5% resistance=10k package=THT]
  R2 = Resistor [tolerance=±5% resistance=220 package=THT]
  J6 = Power [form="♀ (female)" package=THT]
  J4 = AT42qt Touch Sensor [form="♀ (female)" package=THT]
  LED1 = LED [form="♀ (female)" package=THT]
  Q3 = NPN-Transistor [package="TO92 [THT]"]
  R3 = Resistor [tolerance=±5% resistance=10k package=THT]
  Q5 = PNP-Transistor [package="TO92 [THT]"]
  R4 = Resistor [tolerance=±5% resistance=10k package=THT]

nets:
  N1: J5.SCW, PIC18(L)F1.RC5, Part1.D2
  N2: J5.SCL, J1.I2C_SCL, J7.A4
  N3: J5.SDA, J1.I2C_SDA, J7.A5
  VDD: J5.VCC, PIC18(L)F1.VDD, Part1.VCC, J6.VDD, J4.VDD, Q5.E
  GND: J5.GND, PIC18(L)F1.GND, Part1.GND, J1.GND, J8.pin1, J6.GND, J4.GND, LED1.GND, Q3.C
  N4: PIC18(L)F1.RA5, R2.Pin_1
  N5: PIC18(L)F1.RC4, R1.Pin_0
  N6: PIC18(L)F1.RC3, J8.pin2, R1.Pin_1
  N7: PIC18(L)F1.RA2, Part1.A0, J4.OUT
  N8: Part1.A3, R3.Pin_1
  N9: Part1.D13/SCK, J1.SPI-SCK
  N10: Part1.D12/MISO, J1.SPI-MISO
  N11: Part1.D11_PWM/MOSI, J1.SPI_Mosi
  N12: Part1.D10_PWM/SS, J1.EPD_Border_Controll
  N13: Part1.D8, J1.SPI-SSEL
  N14: Part1.D7, J1.EPD_Busy
  N15: Part1.D6_PWM, J1.EPD_RESET
  N16: Part1.D5_PWM, J1.EPD_Panel_Oo
  N17: Part1.D4, J1.EPD_Discharge
  N18: J1.VCC, Q5.C
  N19: R2.Pin_0, LED1.pin2
  N20: Q3.E, R4.Pin_0
  N21: Q3.B, R3.Pin_0
  N22: Q5.B, R4.Pin_1

notes:
  LDR
  EPD
  Power
  DS3232 Clock
  SCL
  SDA
  LED
  TouchSwitch
  NPN
  PNP
  Switch
  Clock
  Touch
  Interrupts
  I2C
  DS3232
  SDA A4
  GND
  VCC

custom parts:
  DS3232 Real Time clock: Generic female header
  PIC16(L)F1824: A DIP stand-in part for whatever IC you want. With 14 pins on a 300mil dual inline package (DIP) footprint.
  Generic female header - 2 pins: Generic female header
  AT42qt Touch Sensor: Generic female header
